// Logisim project B2_Group5.circ as structural Verilog: 1 circuit, main circuit main
module main (
  input  Ground,
  input  Vcc,
  input  _0,
  input  A4,
  input  A3,
  input  A2,
  input  A1,
  input  s2,
  input  s1,
  input  S0,
  input  B4,
  input  B3,
  input  B2,
  input  B1,
  output Cout,
  output S4,
  output S3,
  output S2_2,
  output S1_2,
  output C,
  output S,
  output Z,
  output V
);

  wire main_1_p8, main_1_p13, main_2_p8, main_2_p13, n7404_1_p2, n7404_1_p4, n7404_1_p6, n7404_1_p10,
       n7404_1_p12, n7404_1_p14, n7408_1_p2, n7408_1_p3, n7408_1_p5, n7408_1_p6, n7408_1_p9, n7408_1_p11,
       n7408_1_p13, n7408_1_p14, n7408_2_p1, n7408_2_p7, n7408_2_p12, n7408_2_p15, n7408_3_p6, n7408_3_p11,
       n7408_3_p12, n7408_4_p3, n7408_4_p6, n7408_4_p9, n7408_4_p11, n7408_4_p14, n7408_5_p3, n7408_5_p11,
       n7432_1_p4, n7432_1_p7, n7432_1_p11, n7432_1_p12, n7432_2_p3, n7432_2_p6, n7432_2_p9, n7432_2_p11,
       n7432_2_p12, n7432_2_p14, n7432_3_p3;

  // _7404 7404_1: pin names not known; wires that end beside it: s2, n7404_1_p2, s1, n7404_1_p4, S0, n7404_1_p6, Ground, Vcc, B4, n7404_1_p10, B3, n7404_1_p12, B2, n7404_1_p14
  // _7432 7432_1: pin names not known; wires that end beside it: Vcc, n7404_1_p2, n7404_1_p6, n7432_1_p4, S, S3, n7432_1_p7, Ground, Vcc, S1_2, n7432_1_p11, n7432_1_p12, S2_2, n7432_1_p7, n7432_1_p11
  // _7408 7408_1: pin names not known; wires that end beside it: n7432_1_p4, n7408_1_p2, n7408_1_p3, n7432_1_p4, n7408_1_p5, n7408_1_p6, Ground, Vcc, n7408_1_p9, n7432_1_p4, n7408_1_p11, n7432_1_p4, n7408_1_p13, n7408_1_p14
  // _7408 7408_2: pin names not known; wires that end beside it: n7408_2_p1, S0, s2, n7408_2_p1, n7408_2_p1, n7404_1_p4, n7408_2_p7, Ground, Vcc, n7408_2_p7, n7404_1_p10, n7408_2_p12, n7408_2_p7, n7404_1_p12, n7408_2_p15
  // _7432 7432_2: pin names not known; wires that end beside it: n7408_2_p12, A4, n7432_2_p3, n7408_2_p15, A3, n7432_2_p6, Ground, Vcc, n7432_2_p9, A2, n7432_2_p11, n7432_2_p12, A1, n7432_2_p14
  // _7408 7408_3: pin names not known; wires that end beside it: n7408_2_p7, n7404_1_p14, n7432_2_p9, s1, S0, n7408_3_p6, Ground, Vcc, n7408_3_p6, n7404_1_p2, n7408_3_p11, n7408_3_p12, n7408_2_p7, n7432_2_p12
  // _7400_series_rev1_main main_1: pin names not known; wires that end beside it: n7432_2_p11, n7408_1_p3, Vcc, Vcc, n7408_1_p2, _0, _0, main_1_p8, S2_2, n7408_1_p13, n7408_3_p11, Ground, main_1_p13, n7432_2_p14, S1_2
  // _7486 7486_1: pin names not known; wires that end beside it: B1, Vcc, n7408_3_p12, n7432_1_p12, Vcc, Z, Ground, Vcc, C, n7408_1_p6, V
  // _7408 7408_4: pin names not known; wires that end beside it: s1, n7408_2_p1, n7408_4_p3, n7404_1_p6, n7404_1_p4, n7408_4_p6, Ground, Vcc, n7408_4_p9, n7404_1_p10, n7408_4_p11, n7408_4_p9, n7404_1_p12, n7408_4_p14
  // _7400_series_rev1_main main_2: pin names not known; wires that end beside it: n7432_2_p3, n7408_1_p6, Vcc, Vcc, n7408_1_p5, _0, _0, main_2_p8, S, n7408_1_p9, n7408_1_p14, Ground, main_2_p13, n7432_2_p6, S3
  // _7432 7432_3: pin names not known; wires that end beside it: n7408_4_p3, n7408_4_p6, n7432_3_p3, s2, s1, n7408_4_p9, Ground, Vcc, n7432_3_p3, n7408_4_p11, main_2_p8, n7432_3_p3, n7408_4_p14, main_2_p13
  // _7408 7408_5: pin names not known; wires that end beside it: n7408_4_p9, n7404_1_p14, n7408_5_p3, n7408_1_p11, n7432_1_p4, C, Ground, Vcc, n7408_4_p9, n7408_3_p12, n7408_5_p11
  // _7432 7432_4: pin names not known; wires that end beside it: n7408_5_p3, n7432_3_p3, main_1_p8, n7408_5_p11, n7432_3_p3, main_1_p13, Ground, Vcc

  assign Cout = C;
  assign S4 = S;

  // Notes on the sheet:
  //   ~S2
  //   S2
  //   ~S1
  //   S1
  //   ~S0
  //   S0
  //   Vcc
  //   S4
  //   S3
  //   X4
  //   X3
  //   X2
  //   S2*S0
  //   ~S2 v ~S0
  //   mod1
  //   S2
  //   Y4
  //   X1
  //   C1
  //   Y2
  //   Y3
  //   S1
  //   Y1
  //   1
  //   ~S2 v ~S0
  //   A2
  //   mod1'
  //   A4
  //   CIN
  //   S1!S0!
  //   S2*S1! S0
  //   S2
  //   C2
  //   S2S1S0
  //   ~B1
  //   S1
  //   Mod2
  //   Const
  //   S1+s2
  //   S4
  //   S3
  //   Cout
  //   C3
  //   Register Flag
endmodule
