// Logisim project fpa.circ as structural Verilog: 6 circuits, main circuit main
module main (
  input  [10:0] A,
  input  [10:0] B,
  input  [1:0] op_bunga,
  input  neg,
  output out_5,
  output [12:0] Large_Exponent,
  output [12:0] Difference,
  output [4:0] amount_to_shift
);

  wire comparator_1_lt, n16_bit_alu_1_p6;
  wire [10:0] multiplexer_1_out;
  wire [12:0] negator_1_out;
  wire [15:0] n16_bit_alu_1_p5;

  Comparator #(.width(11), .mode("unsigned")) comparator_1 (
    .a(A), .b(B), .gt(out_5), .lt(comparator_1_lt));  // open: eq
  // _16_Bit_ALU 16_bit_alu_1: pin names not known; wires that end beside it: {{5{1'b0}}, A}, {{5{1'b0}}, B}, neg, op_bunga, n16_bit_alu_1_p5, n16_bit_alu_1_p6, n16_bit_alu_1_p6
  Negator #(.width(13)) negator_1 (.in(n16_bit_alu_1_p5[12:0]), .out(negator_1_out));
  Multiplexer #(.width(11), .enable("false")) multiplexer_1 (
    .in0(A), .in1(B), .out(multiplexer_1_out), .sel(comparator_1_lt));
  Multiplexer #(.width(13), .enable("false")) multiplexer_2 (
    .in0(n16_bit_alu_1_p5[12:0]), .in1(negator_1_out), .out({Difference[12:5], amount_to_shift}),
    .sel(comparator_1_lt));
  assign Large_Exponent = {{2{1'b0}}, multiplexer_1_out};  // Bit_Extender bit_extender_1

  assign Difference[4:0] = amount_to_shift;
endmodule

module adder (
  input  [31:0] A,
  input  [31:0] B,
  output [12:0] Large_Exponent,
  output [31:0] Big_ALU_output,
  output Sign_bit_A,
  output [4:0] Index_of_1,
  output Sign_bit_B,
  output Cout,
  output _3rd_msb_bit
);

  wire n16_bit_alu_with_cin_1_p2;
  wire [31:0] shifter_1_large_input, shifter_1_shifted_smaller;

  shifter shifter_1 (
    .A(A), .B(B), .Shifted_Smaller(shifter_1_shifted_smaller), .Sign_bit_a(Sign_bit_A),
    .sign_bit_b(Sign_bit_B), .Large_Exponent(Large_Exponent), .Large_input(shifter_1_large_input));
  // _16_Bit_ALU_with_Cin 16_bit_alu_with_cin_1: pin names not known; wires that end beside it: shifter_1_large_input[31:16], n16_bit_alu_with_cin_1_p2, shifter_1_shifted_smaller[31:16], 1'b0, 2'b10, {Big_ALU_output[31:30], _3rd_msb_bit, Big_ALU_output[28:16]}, Cout
  // _16_Bit_ALU_with_Cin 16_bit_alu_with_cin_2: pin names not known; wires that end beside it: shifter_1_large_input[15:0], 1'b0, shifter_1_shifted_smaller[15:0], 1'b0, 2'b10, Big_ALU_output[15:0], n16_bit_alu_with_cin_1_p2
  BitFinder #(.width(32), .\type ("high1")) bitfinder_1 (
    .in({Big_ALU_output[31:30], _3rd_msb_bit, Big_ALU_output[28:0]}), .index(Index_of_1));  // open: found

  assign Big_ALU_output[29] = _3rd_msb_bit;
endmodule

module shifter (
  input  [31:0] A,
  input  [31:0] B,
  output [12:0] Large_Exponent,
  output [31:0] Large_input,
  output [31:0] Shifted_Smaller,
  output Sign_bit_a,
  output sign_bit_b
);

  wire main_1_out_5, or_1_out;
  wire [4:0] main_1_amount_to_shift;
  wire [12:0] main_1_difference;
  wire [31:0] multiplexer_1_out, shifter_1_out;

  main main_1 (
    .out_5(main_1_out_5), .A(A[30:20]), .Difference(main_1_difference), .B(B[30:20]),
    .amount_to_shift(main_1_amount_to_shift), .neg(1'b1), .op_bunga(2'b10), .Large_Exponent(Large_Exponent));
  Multiplexer #(.width(32), .enable("false")) multiplexer_1 (
    .in0({4'b0000, A[19:0], {8{1'b0}}}), .in1({4'b0000, B[19:0], {8{1'b0}}}), .out(multiplexer_1_out),
    .sel(main_1_out_5));
  Shifter #(.width(32), .shift("lr")) shifter_1 (
    .in(multiplexer_1_out), .\dist (main_1_amount_to_shift), .out(shifter_1_out));
  Multiplexer #(.width(32), .enable("false")) multiplexer_2 (
    .in0({4'b0000, B[19:0], {8{1'b0}}}), .in1({4'b0000, A[19:0], {8{1'b0}}}), .out(Large_input),
    .sel(main_1_out_5));
  or or_1 (or_1_out, main_1_difference[7], main_1_difference[8], main_1_difference[9], main_1_difference[6], main_1_difference[10], main_1_difference[11], main_1_difference[5]);
  Multiplexer #(.width(32), .enable("false")) multiplexer_3 (
    .in0(shifter_1_out), .in1({32{1'b0}}), .out(Shifted_Smaller), .sel(or_1_out));

  assign Sign_bit_a = A[31];
  assign sign_bit_b = B[31];
endmodule

module Normalizer (
  input  [31:0] A,
  input  [31:0] B,
  output Sign_bit_of_A,
  output [15:0] out_4,
  output [10:0] Shifted_exponent,
  output Sign_bit_of_B,
  output [31:0] Normalized_big_Alu_output,
  output rounder_bit,
  output [31:0] fraction
);

  wire adder_1__3rd_msb_bit, or_1_out;
  wire [4:0] adder_1_index_of_1;
  wire [12:0] adder_1_large_exponent;
  wire [15:0] n16_bit_alu_1_p5, n16_bit_alu_2_p5;
  wire [15:11] multiplexer_2_out;
  wire [31:0] adder_1_big_alu_output, shifter_1_out, shifter_2_out;

  adder adder_1 (
    .Large_Exponent(adder_1_large_exponent), .A(A), .Sign_bit_A(Sign_bit_of_A), .B(B),
    .Index_of_1(adder_1_index_of_1), .Sign_bit_B(Sign_bit_of_B), .Big_ALU_output(adder_1_big_alu_output),
    ._3rd_msb_bit(adder_1__3rd_msb_bit));  // open: Cout
  // _16_Bit_ALU 16_bit_alu_1: pin names not known; wires that end beside it: 16'h1c, {{11{1'b0}}, adder_1_index_of_1}, 1'b1, 2'b10, n16_bit_alu_1_p5
  Shifter #(.width(32), .shift("lr")) shifter_1 (.in(adder_1_big_alu_output), .\dist (5'b00001), .out(shifter_1_out));
  Shifter #(.width(32)) shifter_2 (.in(adder_1_big_alu_output), .\dist (n16_bit_alu_1_p5[4:0]), .out(shifter_2_out));
  Multiplexer #(.width(32), .enable("false")) multiplexer_1 (
    .in0(shifter_2_out), .in1(shifter_1_out),
    .out({Normalized_big_Alu_output[31:29], fraction[20:0], Normalized_big_Alu_output[7:0]}),
    .sel(adder_1__3rd_msb_bit));
  // _16_Bit_ALU 16_bit_alu_2: pin names not known; wires that end beside it: {3'b000, adder_1_large_exponent}, {{11{1'b0}}, n16_bit_alu_1_p5[4:0]}, 1'b1, 2'b10, n16_bit_alu_2_p5
  // _16_Bit_ALU 16_bit_alu_3: pin names not known; wires that end beside it: {3'b000, adder_1_large_exponent}, 16'h1, 1'b0, 2'b10, out_4
  Multiplexer #(.width(16), .enable("false")) multiplexer_2 (
    .in0(n16_bit_alu_2_p5), .in1(out_4), .out({multiplexer_2_out, Shifted_exponent}),
    .sel(adder_1__3rd_msb_bit));
  or or_1 (or_1_out, Normalized_big_Alu_output[6], Normalized_big_Alu_output[7]);
  and and_1 (rounder_bit, or_1_out, fraction[0]);

  assign fraction[31:21] = {11{1'b0}};
  assign Normalized_big_Alu_output[28:8] = fraction[20:0];
endmodule

module rounding (
  input  [31:0] A,
  input  [31:0] B,
  output Sign_bit_of_A,
  output Sign_bit_of_B,
  output [19:0] Final_20_bit_fraction,
  output [10:0] Final_11bit_exponent,
  output carry,
  output sign
);

  wire n16_bit_alu_with_cin_2_c_out, normalizer_1_rounder_bit;
  wire [10:0] normalizer_1_shifted_exponent;
  wire [15:5] n16_bit_alu_with_cin_1_alu_output;
  wire [15:13] n16_bit_alu_1_p5;
  wire [20:0] n16_bit_alu_with_cin_2_alu_output;
  wire [20:20] shifter_1_out;
  wire [31:0] normalizer_1_fraction;

  Normalizer normalizer_1 (
    .A(A), .B(B), .Sign_bit_of_A(Sign_bit_of_A), .Shifted_exponent(normalizer_1_shifted_exponent),
    .Sign_bit_of_B(Sign_bit_of_B), .rounder_bit(normalizer_1_rounder_bit), .fraction(normalizer_1_fraction));  // open: out_4, Normalized_big_Alu_output
  _16_Bit_ALU_with_Cin u_16_bit_alu_with_cin_1 (
    .A(normalizer_1_fraction[31:16]), .B({16{1'b0}}),
    .ALU_Output({n16_bit_alu_with_cin_1_alu_output, n16_bit_alu_with_cin_2_alu_output[20:16]}),
    .Cin(n16_bit_alu_with_cin_2_c_out));  // open: Zero_Flag, Overflow_Flag, C_Out
  _16_Bit_ALU_with_Cin u_16_bit_alu_with_cin_2 (
    .A(normalizer_1_fraction[15:0]), .B({16{1'b0}}), .ALU_Output(n16_bit_alu_with_cin_2_alu_output[15:0]),
    .C_Out(n16_bit_alu_with_cin_2_c_out), .Cin(normalizer_1_rounder_bit));  // open: Zero_Flag, Overflow_Flag
  Shifter #(.width(21), .shift("lr")) shifter_1 (
    .in(n16_bit_alu_with_cin_2_alu_output), .\dist ({4'b0000, n16_bit_alu_with_cin_1_alu_output[5]}),
    .out({shifter_1_out[20], Final_20_bit_fraction}));
  // _16_Bit_ALU 16_bit_alu_1: pin names not known; wires that end beside it: {{5{1'b0}}, normalizer_1_shifted_exponent}, {{15{1'b0}}, n16_bit_alu_with_cin_1_alu_output[5]}, 1'b0, 2'b10, {n16_bit_alu_1_p5, sign, carry, Final_11bit_exponent}
endmodule

module Final_FPA (
  input  [31:0] in_1,
  input  [31:0] in_2,
  output signbit,
  output [19:0] _20_bit_fraction,
  output [10:0] _11_bit_exponent,
  output overflow,
  output underflow
);

  wire rounding_1_carry;

  rounding rounding_1 (
    .A(in_1), .B(in_2), .Sign_bit_of_A(signbit), .Final_20_bit_fraction(_20_bit_fraction),
    .Final_11bit_exponent(_11_bit_exponent), .carry(rounding_1_carry), .sign(underflow));  // open: Sign_bit_of_B
  xor xor_1 (overflow, rounding_1_carry, underflow);
endmodule
