// Logisim project mips.circ as structural Verilog
module Instruction_Memory (
  input  [7:0] Jmp_Address,
  input  [7:0] PC,
  input  [3:0] DstReg_Shmt_Add_Immi_0_3,
  input  [3:0] Src2Reg_DstReg_4_7,
  input  [3:0] Src1Reg_8_11,
  input  [3:0] Opcode_12_15
);

  ROM #(.dataWidth(16)) rom_1 (.addr(PC), .data({Opcode_12_15, Jmp_Address, DstReg_Shmt_Add_Immi_0_3}));  // open: sel

  assign Src1Reg_8_11 = Jmp_Address[7:4];
  assign Src2Reg_DstReg_4_7 = Jmp_Address[3:0];
endmodule
