// Logisim project mips16.circ as structural Verilog: 13 circuits, main circuit main
module main (
  input  in_1,
  output [3:0] zero,
  output [3:0] _0_3,
  output [3:0] out_4,
  output [3:0] _4_7,
  output [3:0] Src1Reg,
  output [3:0] Read_Data_2,
  output [3:0] _8_11,
  output [3:0] Src2Reg,
  output [3:0] Read_Data_1,
  output [3:0] _12_15,
  output [3:0] Dst_Reg,
  output [3:0] Branch_Offset,
  output [7:0] PC,
  output [3:0] zero_2,
  output [3:0] t0,
  output [3:0] t1,
  output [3:0] t2,
  output [3:0] t3,
  output [3:0] t4,
  output [3:0] sp
);

  wire alu_first_1_branchselect, control_ckt_1_alusrc, control_ckt_1_beq, control_ckt_1_bneq,
       control_ckt_1_jmp, control_ckt_1_memread, control_ckt_1_memtoreg, control_ckt_1_memwrite,
       control_ckt_1_regdst, control_ckt_1_regwrite;
  wire [2:0] control_ckt_1_aluop;
  wire [3:0] alu_first_1_output;

  Instructions instructions_1 (
    .CLK(in_1), .BranchSelect(alu_first_1_branchselect), .Jmp(control_ckt_1_jmp),
    .DstReg_Shmt_Add_Immi_0_3(_0_3), .Src2Reg_DstReg_4_7(_4_7), .Src1Reg_8_11(_8_11), .OPcode_12_15(_12_15),
    .PC(PC));
  Control_ckt control_ckt_1 (
    .in_1(_12_15), .Jmp(control_ckt_1_jmp), .RegDst(control_ckt_1_regdst), .RegWrite(control_ckt_1_regwrite),
    .MemRead(control_ckt_1_memread), .MemWrite(control_ckt_1_memwrite), .MemToReg(control_ckt_1_memtoreg),
    .beq(control_ckt_1_beq), .bneq(control_ckt_1_bneq), .ALUsrc(control_ckt_1_alusrc),
    .ALUOp(control_ckt_1_aluop));
  Registers registers_1 (
    .RegDst(control_ckt_1_regdst), .RegWrite(control_ckt_1_regwrite), .DstReg_Shamt_Addr_Immdt_0_3(_0_3),
    .SrcReg2_DstReg_4_7(_4_7), .SrcReg1_8_11(_8_11), .Write_data(out_4), .CLK(in_1),
    .Read_data_1(Read_Data_1), .Read_data_2(Read_Data_1), .zero(zero_2), .t0(t0), .t1(t1), .t2(t2), .t3(t3),
    .t4(t4), .sp(sp));
  ALU_First alu_first_1 (
    .beq(control_ckt_1_beq), .bneq(control_ckt_1_bneq), .ALUsrc(control_ckt_1_alusrc),
    .ALUop(control_ckt_1_aluop), .Read_data_1(Read_Data_1), .Read_data_2(Read_Data_1),
    .DstReg_Shamt_Addr_Immdt_0_3(_0_3), .BranchSelect(alu_first_1_branchselect), .Output(alu_first_1_output));
  Memory_Branch memory_branch_1 (
    .MemToReg(control_ckt_1_memtoreg), .Address(alu_first_1_output), .WriteData(Read_Data_1),
    .MemWrite(control_ckt_1_memwrite), .MemRead(control_ckt_1_memread), .CLK(in_1), .WriteBack(out_4));

  assign Branch_Offset = _0_3;
  assign Dst_Reg = _0_3;
  assign Read_Data_2 = Read_Data_1;
  assign Src1Reg = _8_11;
  assign Src2Reg = _4_7;
endmodule

module Instruction_Memory (
  input  [7:0] PC,
  output [7:0] Jmp_Address,
  output [3:0] DstReg_Shmt_Add_Immi_0_3,
  output [3:0] Src2Reg_DstReg_4_7,
  output [3:0] Src1Reg_8_11,
  output [3:0] Opcode_12_15
);

  ROM #(.dataWidth(16)) rom_1 (.addr(PC), .data({Opcode_12_15, Jmp_Address, DstReg_Shmt_Add_Immi_0_3}));  // open: sel

  assign Src1Reg_8_11 = Jmp_Address[7:4];
  assign Src2Reg_DstReg_4_7 = Jmp_Address[3:0];

  // Notes on the sheet:
  //   contents of rom_1 (hex, n*v repeats v):
  //   3023 4032 3334 d231 e234 f135 1323 331 c431 9160 6441 5334 9150 7131 2531 8225 b352 9160 a319
endmodule

module _4bit_ALU (
  input  [2:0] ALUop,
  input  [3:0] A,
  input  [3:0] B,
  output [3:0] Output,
  output Zero
);

  wire adder4bit_1_p4, adder4bit_2_p3, mux4bit2x1_1_p2, mux4bit2x1_1_p3, mux4bit2x1_1_p4, mux4bit2x1_1_p7,
       mux4bit2x1_4_p2, mux4bit2x1_4_p3, n4bitleftshifter_1_p3, n4bitrightshifter_1_p5, not4bit_1_p2,
       or1bit4x1_1_p2;
  wire [3:0] and_1_out, nor_1_out, or_1_out;

  // Adder4bit adder4bit_1: pin names not known; wires that end beside it: A, B, 1'b0, adder4bit_1_p4
  // NOT4bit not4bit_1: pin names not known; wires that end beside it: B, not4bit_1_p2, not4bit_1_p2
  // Adder4bit adder4bit_2: pin names not known; wires that end beside it: A, 1'b1, adder4bit_2_p3
  assign or_1_out = A | B;  // OR_Gate or_1, 4 bits wide
  assign and_1_out = A & B;  // AND_Gate and_1, 4 bits wide
  assign nor_1_out = ~(A | B);  // NOR_Gate nor_1, 4 bits wide
  // _4bitLeftShifter 4bitleftshifter_1: pin names not known; wires that end beside it: A, B, n4bitleftshifter_1_p3
  // _4bitRightShifter 4bitrightshifter_1: pin names not known; wires that end beside it: B, A, A, B, n4bitrightshifter_1_p5
  // MUX4bit2x1 mux4bit2x1_1: pin names not known; wires that end beside it: ALUop[1], mux4bit2x1_1_p2, mux4bit2x1_1_p3, mux4bit2x1_1_p4, ALUop[2], mux4bit2x1_1_p4, mux4bit2x1_1_p7
  // MUX4bit2x1 mux4bit2x1_2: pin names not known; wires that end beside it: ALUop[0], adder4bit_1_p4, adder4bit_2_p3, mux4bit2x1_1_p2
  // MUX4bit2x1 mux4bit2x1_3: pin names not known; wires that end beside it: ALUop[0], or_1_out, and_1_out, mux4bit2x1_1_p3
  // MUX4bit2x1 mux4bit2x1_4: pin names not known; wires that end beside it: ALUop[1], mux4bit2x1_4_p2, mux4bit2x1_4_p3, mux4bit2x1_1_p7
  // MUX4bit2x1 mux4bit2x1_5: pin names not known; wires that end beside it: ALUop[0], nor_1_out, n4bitleftshifter_1_p3, mux4bit2x1_4_p2
  // MUX4bit2x1 mux4bit2x1_6: pin names not known; wires that end beside it: ALUop[0], n4bitrightshifter_1_p5, 4'b0000, mux4bit2x1_4_p3
  // MUX4bit2x1 mux4bit2x1_7: pin names not known; wires that end beside it: Output
  // NOT1bit not1bit_1: pin names not known; wires that end beside it: Zero
  // OR1bit4x1 or1bit4x1_1: pin names not known; wires that end beside it: Output, or1bit4x1_1_p2, or1bit4x1_1_p2

  // Notes on the sheet:
  //   000 Add
  //   001 Sub
  //   010 And
  //   011 Or
  //   100 Nor
  //   101 SL
  //   110 SR
  //   111 Zero
endmodule

// Control
module Control_ckt (
  input  [3:0] in_1,
  output Jmp,
  output RegDst,
  output RegWrite,
  output MemRead,
  output MemWrite,
  output MemToReg,
  output beq,
  output bneq,
  output ALUsrc,
  output [2:0] ALUOp
);

  ROM #(.addrWidth(4), .dataWidth(12)) rom_1 (
    .addr(in_1), .data({ALUOp, ALUsrc, bneq, beq, MemToReg, MemWrite, MemRead, RegWrite, RegDst, Jmp}),
    .sel(1'b1));
endmodule

module RequiredRegisters (
  input  [3:0] in_zero,
  input  CLKzero,
  input  [3:0] in_t0,
  input  CLK0,
  input  [3:0] in_t1,
  input  CLK1,
  input  [3:0] in_t2,
  input  CLK2,
  input  [3:0] in_t3,
  input  CLK3,
  input  [3:0] in_t4,
  input  CLK4,
  input  [3:0] in_sp,
  input  CLKsp,
  output [3:0] zero,
  output [3:0] t0,
  output [3:0] t1,
  output [3:0] t2,
  output [3:0] t3,
  output [3:0] t4,
  output [3:0] sp
);

  wire [3:0] n7474_1_p4;

  // _7474 7474_1: pin names not known; wires that end beside it: 1'b0, in_zero[0], CLKzero, n7474_1_p4[0], 1'b1, in_zero[1], CLKzero, n7474_1_p4[1]
  // _7474 7474_2: pin names not known; wires that end beside it: 1'b0, in_zero[2], CLKzero, n7474_1_p4[2], 1'b1, in_zero[3], CLKzero
  // _7474 7474_3: pin names not known; wires that end beside it: 1'b0, in_t0[0], CLK0, t0[0], n7474_1_p4[3], 1'b1, in_t0[1], CLK0, t0[1]
  // _7474 7474_4: pin names not known; wires that end beside it: 1'b0, in_t0[2], CLK0, t0[2], 1'b1, in_t0[3], CLK0
  // _7474 7474_5: pin names not known; wires that end beside it: 1'b0, in_t1[0], CLK1, t1[0], t0[3], 1'b1, in_t1[1], CLK1, t1[1]
  // _7474 7474_6: pin names not known; wires that end beside it: 1'b0, in_t1[2], CLK1, t1[2], 1'b1, in_t1[3], CLK1, t1[3]
  // _7474 7474_7: pin names not known; wires that end beside it: 1'b0, in_t2[0], CLK2, t2[0], 1'b1, in_t2[1], CLK2
  // _7474 7474_8: pin names not known; wires that end beside it: 1'b0, in_t2[2], CLK2, t2[2], t2[1], 1'b1, in_t2[3], CLK2
  // _7474 7474_9: pin names not known; wires that end beside it: 1'b0, in_t3[0], CLK3, t3[0], t2[3], 1'b1, in_t3[1], CLK3, t3[1]
  // _7474 7474_10: pin names not known; wires that end beside it: 1'b0, in_t3[2], CLK3, t3[2], 1'b1, in_t3[3], CLK3
  // _7474 7474_11: pin names not known; wires that end beside it: 1'b0, in_t4[0], CLK4, t4[0], t3[3], 1'b1, in_t4[1], CLK4, t4[1]
  // _7474 7474_12: pin names not known; wires that end beside it: 1'b0, in_t4[2], CLK4, t4[2], 1'b1, in_t4[3], CLK4, t4[3]
  // _7474 7474_13: pin names not known; wires that end beside it: 1'b0, in_sp[0], CLKsp, sp[0], 1'b1, in_sp[1], CLKsp
  // _7474 7474_14: pin names not known; wires that end beside it: 1'b0, in_sp[2], CLKsp, sp[2], 1'b0, sp[1], 1'b1, in_sp[3], CLKsp, sp[3], 1'b1

  assign zero = 4'b0000;
endmodule

module RegisterFile (
  input  [3:0] Reg1Address,
  input  [3:0] Reg2Address,
  input  [3:0] Write_Data,
  input  [3:0] WriteRegAddress,
  input  RegWrite,
  input  Clk,
  output [3:0] Read_Data_1,
  output [3:0] Read_Data_2,
  output [3:0] zero,
  output [3:0] t0,
  output [3:0] t1,
  output [3:0] t2,
  output [3:0] t3,
  output [3:0] t4,
  output [3:0] sp
);

  wire and_1_out, decoder_1_out1, decoder_1_out2, decoder_1_out3, decoder_1_out4, decoder_1_out5,
       decoder_1_out6;
  wire [2:0] multiplexer_1_out;

  Multiplexer #(.width(3), .enable("false")) multiplexer_1 (
    .in0(3'b000), .in1(WriteRegAddress[2:0]), .out(multiplexer_1_out), .sel(and_1_out));
  and and_1 (and_1_out, RegWrite, Clk);
  Decoder #(.select(3), .enable("false")) decoder_1 (
    .out1(decoder_1_out1), .out2(decoder_1_out2), .out3(decoder_1_out3), .out4(decoder_1_out4),
    .out5(decoder_1_out5), .out6(decoder_1_out6), .sel(multiplexer_1_out));  // open: out0, out7
  // _4_bit_MIPS_Registers registers_1: pin names not known; wires that end beside it: Write_Data, decoder_1_out1, Write_Data, decoder_1_out2, Write_Data, decoder_1_out3, Write_Data, decoder_1_out4, Write_Data, decoder_1_out5, Write_Data, decoder_1_out6, zero, t0, t1, t2, t3, t4, sp
  Multiplexer #(.select(3), .width(4), .enable("false")) multiplexer_2 (
    .in0(zero), .in1(t0), .in2(t1), .in3(t2), .in4(t3), .in5(t4), .in6(sp), .out(Read_Data_1),
    .sel(Reg1Address[2:0]));  // open: in7
  Multiplexer #(.select(3), .width(4), .enable("false")) multiplexer_3 (
    .in0(zero), .in1(t0), .in2(t1), .in3(t2), .in4(t3), .in5(t4), .in6(sp), .out(Read_Data_2),
    .sel(Reg2Address[2:0]));  // open: in7
endmodule

module MemoryData (
  input  [3:0] Address,
  input  [3:0] WriteData,
  input  MemWrite,
  input  MemRead,
  input  CLK,
  output [3:0] MemData
);

  RAM #(.addrWidth(4), .dataWidth(4), .bus("separate")) ram_1 (
    .addr(Address), .din(WriteData), .data(MemData), .str(MemWrite), .clk(CLK), .ld(MemRead));  // open: sel, clr
endmodule

module Reg_8bit (
  input  [7:0] in,
  input  CLK0,
  output [7:0] out
);

  // _7474 7474_1: pin names not known; wires that end beside it: 1'b0, in[0], CLK0, out[0], 1'b1, in[1], CLK0, out[1]
  // _7474 7474_2: pin names not known; wires that end beside it: 1'b0, in[2], CLK0, out[2], 1'b1, in[3], CLK0, out[3]
  // _7474 7474_3: pin names not known; wires that end beside it: 1'b0, in[4], CLK0, out[4], 1'b1, in[5], CLK0
  // _7474 7474_4: pin names not known; wires that end beside it: 1'b0, in[6], CLK0, out[6], 1'b0, out[5], 1'b1, in[7], CLK0, out[7]
endmodule

module ALU_for_branching (
  input  [7:0] PC_add,
  input  [3:0] Branch_add,
  output [7:0] Output_Ins_address
);

  wire [7:0] adder_1_out, negator_1_out, subtractor_1_out;

  Negator negator_1 (.in({{5{Branch_add[3]}}, Branch_add[2:0]}), .out(negator_1_out));
  Subtractor subtractor_1 (.a(PC_add), .b(negator_1_out), .out(subtractor_1_out));  // open: bin, bout
  Adder adder_1 (.a(PC_add), .b({{5{Branch_add[3]}}, Branch_add[2:0]}), .out(adder_1_out));  // open: cin, cout
  Multiplexer #(.width(8), .enable("false")) multiplexer_1 (
    .in0(adder_1_out), .in1(subtractor_1_out), .out(Output_Ins_address), .sel(Branch_add[3]));
endmodule

// Memory
module Memory_Branch (
  input  MemToReg,
  input  [3:0] Address,
  input  [3:0] WriteData,
  input  MemWrite,
  input  MemRead,
  input  CLK,
  output [3:0] WriteBack
);

  wire [3:0] memorydata_1_memdata;

  MemoryData memorydata_1 (
    .Address(Address), .WriteData(WriteData), .MemWrite(MemWrite), .MemRead(MemRead), .CLK(CLK),
    .MemData(memorydata_1_memdata));
  Multiplexer #(.width(4), .enable("false")) multiplexer_1 (
    .in0(Address), .in1(memorydata_1_memdata), .out(WriteBack), .sel(MemToReg));
endmodule

// ALU
module ALU_First (
  input  beq,
  input  bneq,
  input  ALUsrc,
  input  [2:0] ALUop,
  input  [3:0] Read_data_1,
  input  [3:0] Read_data_2,
  input  [3:0] DstReg_Shamt_Addr_Immdt_0_3,
  output BranchSelect,
  output [3:0] Output
);

  wire n4bit_alu_1_zero, n7408_1_p3, n7408_1_p5, n7408_1_p6;
  wire [3:0] multiplexer_1_out;

  Multiplexer #(.width(4), .enable("false")) multiplexer_1 (
    .in0(Read_data_2), .in1(DstReg_Shamt_Addr_Immdt_0_3), .out(multiplexer_1_out), .sel(ALUsrc));
  _4bit_ALU u_4bit_alu_1 (
    .ALUop(ALUop), .A(Read_data_1), .B(multiplexer_1_out), .Output(Output), .Zero(n4bit_alu_1_zero));
  // _7408 7408_1: pin names not known; wires that end beside it: beq, n4bit_alu_1_zero, n7408_1_p3, bneq, n7408_1_p5, n7408_1_p6
  not not_1 (n7408_1_p5, n4bit_alu_1_zero);
  or or_1 (BranchSelect, n7408_1_p6, n7408_1_p3);
endmodule

// RegisterFile
module Registers (
  input  RegDst,
  input  RegWrite,
  input  [3:0] DstReg_Shamt_Addr_Immdt_0_3,
  input  [3:0] SrcReg2_DstReg_4_7,
  input  [3:0] SrcReg1_8_11,
  input  [3:0] Write_data,
  input  CLK,
  output [3:0] Read_data_1,
  output [3:0] Read_data_2,
  output [3:0] zero,
  output [3:0] t0,
  output [3:0] t1,
  output [3:0] t2,
  output [3:0] t3,
  output [3:0] t4,
  output [3:0] sp
);

  wire [3:0] multiplexer_1_out;

  Multiplexer #(.width(4), .enable("false")) multiplexer_1 (
    .in0(SrcReg2_DstReg_4_7), .in1(DstReg_Shamt_Addr_Immdt_0_3), .out(multiplexer_1_out), .sel(RegDst));
  RegisterFile registerfile_1 (
    .Reg1Address(SrcReg1_8_11), .Reg2Address(SrcReg2_DstReg_4_7), .Write_Data(Write_data),
    .WriteRegAddress(multiplexer_1_out), .RegWrite(RegWrite), .Clk(CLK), .Read_Data_1(Read_data_1),
    .Read_Data_2(Read_data_2), .zero(zero), .t0(t0), .t1(t1), .t2(t2), .t3(t3), .t4(t4), .sp(sp));
endmodule

// Instruction
module Instructions (
  input  CLK,
  input  BranchSelect,
  input  Jmp,
  output [3:0] DstReg_Shmt_Add_Immi_0_3,
  output [3:0] Src2Reg_DstReg_4_7,
  output [3:0] Src1Reg_8_11,
  output [3:0] OPcode_12_15,
  output [7:0] PC
);

  wire n7474_1_p3, not_1_out;
  wire [7:0] adder_1_out, alu_for_branching_1_output_ins_address, instruction_memory_1_jmp_address,
       multiplexer_2_out, multiplexer_3_out, reg_8bit_1_out;

  not not_1 (not_1_out, CLK);
  Reg_8bit reg_8bit_1 (.in(multiplexer_3_out), .CLK0(not_1_out), .out(reg_8bit_1_out));
  Multiplexer #(.width(8), .enable("false")) multiplexer_1 (
    .in0({8{1'b0}}), .in1(reg_8bit_1_out), .out(PC), .sel(n7474_1_p3));
  // _7474 7474_1: pin names not known; wires that end beside it: 1'b1, CLK, n7474_1_p3, 1'b0, 1'b1
  Adder adder_1 (.a(PC), .b({8{1'b0}}), .out(adder_1_out), .cin(1'b1));  // open: cout
  Instruction_Memory instruction_memory_1 (
    .PC(PC), .Jmp_Address(instruction_memory_1_jmp_address),
    .DstReg_Shmt_Add_Immi_0_3(DstReg_Shmt_Add_Immi_0_3), .Src2Reg_DstReg_4_7(Src2Reg_DstReg_4_7),
    .Src1Reg_8_11(Src1Reg_8_11), .Opcode_12_15(OPcode_12_15));
  ALU_for_branching alu_for_branching_1 (
    .PC_add(adder_1_out), .Branch_add(DstReg_Shmt_Add_Immi_0_3),
    .Output_Ins_address(alu_for_branching_1_output_ins_address));
  Multiplexer #(.width(8), .enable("false")) multiplexer_2 (
    .in0(adder_1_out), .in1(alu_for_branching_1_output_ins_address), .out(multiplexer_2_out),
    .sel(BranchSelect));
  Multiplexer #(.width(8), .enable("false")) multiplexer_3 (
    .in0(multiplexer_2_out), .in1(instruction_memory_1_jmp_address), .out(multiplexer_3_out), .sel(Jmp));
endmodule
