// Logisim project mips2.circ as structural Verilog
module Instruction_Memory (
  input  [7:0] Jmp_Address,
  input  [7:0] PC,
  input  [3:0] DstReg_Shmt_Add_Immi_0_3,
  input  [3:0] Src2Reg_DstReg_4_7,
  input  [3:0] Src1Reg_8_11,
  input  [3:0] Opcode_12_15
);

  ROM #(.dataWidth(16)) rom_1 (.addr(PC), .data({Opcode_12_15, Jmp_Address, DstReg_Shmt_Add_Immi_0_3}));  // open: sel

  assign Src1Reg_8_11 = Jmp_Address[7:4];
  assign Src2Reg_DstReg_4_7 = Jmp_Address[3:0];
endmodule

module _4bit_ALU (
  input  [2:0] ALUop,
  input  [3:0] A,
  input  [3:0] B,
  output [3:0] Out,
  output Zero
);

  wire adder4bit_1_p4, adder4bit_2_p3, mux4bit2x1_1_p4, mux4bit2x1_1_p7, mux4bit2x1_2_p1, mux4bit2x1_2_p4,
       mux4bit2x1_4_p4, mux4bit2x1_4_p7, n4bitleftshifter_1_p3, n4bitrightshifter_1_p5, not4bit_1_p2,
       or1bit4x1_1_p2;
  wire [3:0] and_1_out, nor_1_out, or_1_out;

  // Adder4bit adder4bit_1: pin names not known; wires that end beside it: A, B, 1'b0, adder4bit_1_p4
  // NOT4bit not4bit_1: pin names not known; wires that end beside it: B, not4bit_1_p2, not4bit_1_p2
  // Adder4bit adder4bit_2: pin names not known; wires that end beside it: A, 1'b1, adder4bit_2_p3
  assign or_1_out = A | B;  // OR_Gate or_1, 4 bits wide
  assign and_1_out = A & B;  // AND_Gate and_1, 4 bits wide
  assign nor_1_out = ~(A | B);  // NOR_Gate nor_1, 4 bits wide
  // _4bitLeftShifter 4bitleftshifter_1: pin names not known; wires that end beside it: A, B, n4bitleftshifter_1_p3
  // _4bitRightShifter 4bitrightshifter_1: pin names not known; wires that end beside it: B, A, A, B, n4bitrightshifter_1_p5
  // MUX4bit2x1 mux4bit2x1_1: pin names not known; wires that end beside it: ALUop[0], adder4bit_1_p4, adder4bit_2_p3, mux4bit2x1_1_p4, ALUop[1], mux4bit2x1_1_p4, mux4bit2x1_1_p7
  // MUX4bit2x1 mux4bit2x1_2: pin names not known; wires that end beside it: mux4bit2x1_2_p1, ALUop[2], mux4bit2x1_2_p1, mux4bit2x1_2_p4
  // MUX4bit2x1 mux4bit2x1_3: pin names not known; wires that end beside it: ALUop[0], or_1_out, and_1_out, mux4bit2x1_1_p7
  // MUX4bit2x1 mux4bit2x1_4: pin names not known; wires that end beside it: ALUop[0], nor_1_out, n4bitleftshifter_1_p3, mux4bit2x1_4_p4, ALUop[1], mux4bit2x1_4_p4, mux4bit2x1_4_p7
  // MUX4bit2x1 mux4bit2x1_5: pin names not known; wires that end beside it: mux4bit2x1_2_p4
  // MUX4bit2x1 mux4bit2x1_6: pin names not known; wires that end beside it: ALUop[0], n4bitrightshifter_1_p5, 4'b0000, mux4bit2x1_4_p7
  // MUX4bit2x1 mux4bit2x1_7: pin names not known; wires that end beside it: Out
  // NOT1bit not1bit_1: pin names not known; wires that end beside it: Zero
  // OR1bit4x1 or1bit4x1_1: pin names not known; wires that end beside it: Out, or1bit4x1_1_p2, or1bit4x1_1_p2

  // Notes on the sheet:
  //   000 Add
  //   001 Sub
  //   010 And
  //   011 Or
  //   100 Nor
  //   101 SL
  //   110 SR
  //   111 Zero
endmodule

module Control_ckt (
  input  [3:0] in_1,
  output Jmp
);

  wire [11:1] rom_1_data;

  ROM #(.addrWidth(4), .dataWidth(12)) rom_1 (.addr(in_1), .data({rom_1_data, Jmp}), .sel(1'b1));
endmodule
